// Logisim project 171044032_Final_project.circ as structural Verilog: 12 circuits, main circuit main
module main (
  input  [7:0] I0,
  input  [7:0] I1,
  input  [7:0] I2,
  input  [7:0] I3,
  input  [7:0] I4,
  input  [7:0] I5,
  input  [7:0] I6,
  input  [7:0] I7,
  output [4:0] state
);

  wire a_out, b_out, c_out, clock_1_out, d_out, e_out, f_out, g_out, go_out, h_out, hangman_fsm_1_l_count,
       hangman_fsm_1_reset_tty, hangman_fsm_1_take_input, hangman_fsm_1_write_tty, i_out, j_out, k_out,
       l_out, m_out, mykeyboard_1_getinput, n7segmentdisplay_1_b, n7segmentdisplay_1_bl,
       n7segmentdisplay_1_br, n7segmentdisplay_1_m, n7segmentdisplay_1_u, n7segmentdisplay_1_ul,
       n7segmentdisplay_1_ur, n7segmentdisplay_2_b, n7segmentdisplay_2_bl, n7segmentdisplay_2_br,
       n7segmentdisplay_2_m, n7segmentdisplay_2_u, n7segmentdisplay_2_ul, n7segmentdisplay_2_ur,
       n7segmentdisplay_3_b, n7segmentdisplay_3_bl, n7segmentdisplay_3_br, n7segmentdisplay_3_m,
       n7segmentdisplay_3_u, n7segmentdisplay_3_ul, n7segmentdisplay_3_ur, n_out, o_out, p_out, q_out, r_out,
       RESET_out, s_out, t_out, u_out, v_out, w_out, x_out, y_out, z_out;
  wire [3:0] hangman_fsm_1_computer, hangman_fsm_1_letter_count, hangman_fsm_1_player, hangman_fsm_1_tries;
  wire [6:0] hangman_fsm_1_input_tty, ledmatrix_1_o0, ledmatrix_1_o1, ledmatrix_1_o2, ledmatrix_1_o3,
       ledmatrix_1_o4, mykeyboard_1_i_guess;

  Clock clock_1 (.out(clock_1_out));
  Button go (.out(go_out));
  Button b (.out(b_out));
  Button a (.out(a_out));
  Button e (.out(e_out));
  Button d (.out(d_out));
  Button c (.out(c_out));
  Button g (.out(g_out));
  Button f (.out(f_out));
  DotMatrix dotmatrix_1 (
    .col0(ledmatrix_1_o0), .col1(ledmatrix_1_o1), .col2(ledmatrix_1_o2), .col3(ledmatrix_1_o3),
    .col4(ledmatrix_1_o4));
  LedMatrix ledmatrix_1 (
    .Input(hangman_fsm_1_tries), .O0(ledmatrix_1_o0), .O1(ledmatrix_1_o1), .O2(ledmatrix_1_o2),
    .O3(ledmatrix_1_o3), .O4(ledmatrix_1_o4));
  Button h (.out(h_out));
  Button i (.out(i_out));
  Button j (.out(j_out));
  TTY #(.rows(1), .cols(8)) tty_1 (
    .data(hangman_fsm_1_input_tty), .clk(clock_1_out), .we(hangman_fsm_1_write_tty),
    .clr(hangman_fsm_1_reset_tty));
  Button m (.out(m_out));
  Button k (.out(k_out));
  Button l (.out(l_out));
  _7SegmentDisplay u_7segmentdisplay_1 (
    .State(hangman_fsm_1_letter_count), .Load(hangman_fsm_1_l_count), .clk(clock_1_out),
    .M(n7segmentdisplay_1_m), .UL(n7segmentdisplay_1_ul), .U(n7segmentdisplay_1_u),
    .UR(n7segmentdisplay_1_ur), .BR(n7segmentdisplay_1_br), .B(n7segmentdisplay_1_b),
    .BL(n7segmentdisplay_1_bl));  // open: Reset
  Hangman_FSM hangman_fsm_1 (
    .go(go_out), .I0(I0), .I1(I1), .I2(I2), .I3(I3), .I4(I4), .I5(I5), .I6(I6), .I7(I7),
    .I_guess(mykeyboard_1_i_guess), .L_guess(mykeyboard_1_getinput), .clk(clock_1_out),
    .Reset_Count(RESET_out), .Tries(hangman_fsm_1_tries), .Letter_Count(hangman_fsm_1_letter_count),
    .L_count(hangman_fsm_1_l_count), .Player(hangman_fsm_1_player), .Computer(hangman_fsm_1_computer),
    .Input_TTY(hangman_fsm_1_input_tty), .Write_TTY(hangman_fsm_1_write_tty),
    .Reset_TTY(hangman_fsm_1_reset_tty), .take_input(hangman_fsm_1_take_input), .state(state));
  Button o (.out(o_out));
  Button n (.out(n_out));
  _7_Segment_Display u_7_segment_display_1 (
    .g(n7segmentdisplay_1_m), .f(n7segmentdisplay_1_ul), .a(n7segmentdisplay_1_u), .b(n7segmentdisplay_1_ur),
    .e(n7segmentdisplay_1_bl), .d(n7segmentdisplay_1_b), .c(n7segmentdisplay_1_br));  // open: dp
  MyKeyboard mykeyboard_1 (
    .I_Guess(mykeyboard_1_i_guess), .getInput(mykeyboard_1_getinput), .a(a_out), .b(b_out), .c(c_out),
    .d(d_out), .e(e_out), .f(f_out), .g(g_out), .h(h_out), .i(i_out), .j(j_out), .k(k_out), .l(l_out),
    .m(m_out), .n(n_out), .o(o_out), .p(p_out), .q(q_out), .r(r_out), .s(s_out), .t(t_out), .u(u_out),
    .v(v_out), .w(w_out), .x(x_out), .y(y_out), .z(z_out), .take_input(hangman_fsm_1_take_input));
  Button p (.out(p_out));
  Button r (.out(r_out));
  Button q (.out(q_out));
  _7SegmentDisplay u_7segmentdisplay_2 (
    .State(hangman_fsm_1_player), .Load(1'b1), .clk(clock_1_out), .M(n7segmentdisplay_2_m),
    .UL(n7segmentdisplay_2_ul), .U(n7segmentdisplay_2_u), .UR(n7segmentdisplay_2_ur),
    .BR(n7segmentdisplay_2_br), .B(n7segmentdisplay_2_b), .BL(n7segmentdisplay_2_bl));  // open: Reset
  _7SegmentDisplay u_7segmentdisplay_3 (
    .State(hangman_fsm_1_computer), .Load(1'b1), .clk(clock_1_out), .M(n7segmentdisplay_3_m),
    .UL(n7segmentdisplay_3_ul), .U(n7segmentdisplay_3_u), .UR(n7segmentdisplay_3_ur),
    .BR(n7segmentdisplay_3_br), .B(n7segmentdisplay_3_b), .BL(n7segmentdisplay_3_bl));  // open: Reset
  Button s (.out(s_out));
  Button u (.out(u_out));
  Button t (.out(t_out));
  _7_Segment_Display u_7_segment_display_2 (
    .g(n7segmentdisplay_2_m), .f(n7segmentdisplay_2_ul), .a(n7segmentdisplay_2_u), .b(n7segmentdisplay_2_ur),
    .e(n7segmentdisplay_2_bl), .d(n7segmentdisplay_2_b), .c(n7segmentdisplay_2_br));  // open: dp
  _7_Segment_Display u_7_segment_display_3 (
    .g(n7segmentdisplay_3_m), .f(n7segmentdisplay_3_ul), .a(n7segmentdisplay_3_u), .b(n7segmentdisplay_3_ur),
    .e(n7segmentdisplay_3_bl), .d(n7segmentdisplay_3_b), .c(n7segmentdisplay_3_br));  // open: dp
  Button v (.out(v_out));
  Button w (.out(w_out));
  Button x (.out(x_out));
  Button y (.out(y_out));
  Button z (.out(z_out));
  Button RESET (.out(RESET_out));

  // Notes on the sheet:
  //   TRIES
  //   I tested at 128Hz frequency
  //   LETTERS
  //   User
  //   Machine
endmodule

module Hangman_FSM (
  input  go,
  input  [7:0] I0,
  input  [7:0] I1,
  input  [7:0] I2,
  input  [7:0] I3,
  input  [7:0] I4,
  input  [7:0] I5,
  input  [7:0] I6,
  input  [7:0] I7,
  input  [6:0] I_guess,
  input  L_guess,
  input  clk,
  input  Reset_Count,
  output [3:0] Tries,
  output [3:0] Letter_Count,
  output L_count,
  output [3:0] Player,
  output [3:0] Computer,
  output [6:0] Input_TTY,
  output Write_TTY,
  output Reset_TTY,
  output take_input,
  output [4:0] state
);

  wire hangman_controlunit_1_comp_inc, hangman_controlunit_1_l_chars, hangman_controlunit_1_l_count_letters,
       hangman_controlunit_1_l_found, hangman_controlunit_1_l_i, hangman_controlunit_1_l_inputc,
       hangman_controlunit_1_l_isfound, hangman_controlunit_1_l_try, hangman_controlunit_1_player_inc,
       hangman_controlunit_1_r_i, hangman_controlunit_1_r_isfound, hangman_controlunit_1_r_try,
       hangman_controlunit_1_s_char, hangman_controlunit_1_s_count_letters, hangman_controlunit_1_s_found,
       hangman_controlunit_1_s_i, hangman_data_1_found, hangman_data_1_i_lt8, hangman_data_1_isfound_i,
       hangman_data_1_try_lt10, hangman_data_1_word_i_eq0, hangman_data_1_word_i_eqinput;
  wire [2:0] hangman_data_1_computer_count, hangman_data_1_player_count;
  wire [7:7] hangman_data_1_tty;

  Hangman_Data hangman_data_1 (
    .I_inputC({1'b0, I_guess}), .L_inputC(hangman_controlunit_1_l_inputc), .I0(I0), .I1(I1), .I2(I2),
    .I3(I3), .I4(I4), .I5(I5), .I6(I6), .I7(I7), .L_chars(hangman_controlunit_1_l_chars),
    .R_isFound(hangman_controlunit_1_r_isfound), .L_isFound(hangman_controlunit_1_l_isfound),
    .R_try(hangman_controlunit_1_r_try), .L_try(hangman_controlunit_1_l_try),
    .L_count_letters(hangman_controlunit_1_l_count_letters),
    .S_count_letters(hangman_controlunit_1_s_count_letters), .L_i(hangman_controlunit_1_l_i),
    .S_i(hangman_controlunit_1_s_i), .R_i(hangman_controlunit_1_r_i),
    .L_found(hangman_controlunit_1_l_found), .S_found(hangman_controlunit_1_s_found),
    .Player_Inc(hangman_controlunit_1_player_inc), .Comp_Inc(hangman_controlunit_1_comp_inc),
    .S_char(hangman_controlunit_1_s_char), .reset_count(Reset_Count), .clk(clk),
    .word_i_eqInput(hangman_data_1_word_i_eqinput), .found(hangman_data_1_found),
    .word_i_eq0(hangman_data_1_word_i_eq0), .isFound_i(hangman_data_1_isfound_i),
    .try_lt10(hangman_data_1_try_lt10), .Try_Count(Tries), .Letter_Count(Letter_Count),
    .i_lt8(hangman_data_1_i_lt8), .Player_Count(hangman_data_1_player_count),
    .Computer_Count(hangman_data_1_computer_count), .TTY({hangman_data_1_tty[7], Input_TTY}));
  Hangman_ControlUnit hangman_controlunit_1 (
    .go(go), .getInput(L_guess), .word_i_eqInput(hangman_data_1_word_i_eqinput),
    .found(hangman_data_1_found), .word_i_eq0(hangman_data_1_word_i_eq0),
    .isFound_i(hangman_data_1_isfound_i), .try_lt10(hangman_data_1_try_lt10), .i_lt8(hangman_data_1_i_lt8),
    .clk(clk), .L_inputC(hangman_controlunit_1_l_inputc), .L_chars(hangman_controlunit_1_l_chars),
    .R_isFound(hangman_controlunit_1_r_isfound), .L_isFound(hangman_controlunit_1_l_isfound),
    .R_try(hangman_controlunit_1_r_try), .L_try(hangman_controlunit_1_l_try),
    .L_count_letters(hangman_controlunit_1_l_count_letters),
    .S_count_letters(hangman_controlunit_1_s_count_letters), .L_i(hangman_controlunit_1_l_i),
    .S_i(hangman_controlunit_1_s_i), .R_i(hangman_controlunit_1_r_i),
    .L_found(hangman_controlunit_1_l_found), .S_found(hangman_controlunit_1_s_found),
    .Player_Inc(hangman_controlunit_1_player_inc), .Comp_inc(hangman_controlunit_1_comp_inc),
    .S_char(hangman_controlunit_1_s_char), .write(Write_TTY), .R_TTY(Reset_TTY), .Display_7seg(L_count),
    .take_input(take_input), .REGISTER(state));
  assign Player = {{1{1'b0}}, hangman_data_1_player_count};  // Bit_Extender bit_extender_1
  assign Computer = {{1{1'b0}}, hangman_data_1_computer_count};  // Bit_Extender bit_extender_2
endmodule

module Hangman_Data (
  input  [7:0] I_inputC,
  input  L_inputC,
  input  [7:0] I0,
  input  [7:0] I1,
  input  [7:0] I2,
  input  [7:0] I3,
  input  [7:0] I4,
  input  [7:0] I5,
  input  [7:0] I6,
  input  [7:0] I7,
  input  L_chars,
  input  R_isFound,
  input  L_isFound,
  input  R_try,
  input  L_try,
  input  L_count_letters,
  input  S_count_letters,
  input  L_i,
  input  S_i,
  input  R_i,
  input  L_found,
  input  S_found,
  input  Player_Inc,
  input  Comp_Inc,
  input  S_char,
  input  reset_count,
  input  clk,
  output word_i_eqInput,
  output found,
  output word_i_eq0,
  output isFound_i,
  output try_lt10,
  output [3:0] Try_Count,
  output [3:0] Letter_Count,
  output i_lt8,
  output [2:0] Player_Count,
  output [2:0] Computer_Count,
  output [7:0] TTY
);

  wire and_1_out, and_2_out, and_3_out, and_4_out, and_5_out, and_6_out, and_7_out, and_8_out,
       demultiplexer_1_out0, demultiplexer_1_out1, demultiplexer_1_out2, demultiplexer_1_out3,
       demultiplexer_1_out4, demultiplexer_1_out5, demultiplexer_1_out6, demultiplexer_1_out7, isFound_0_q,
       isFound_1_q, isFound_2_q, isFound_3_q, isFound_4_q, isFound_5_q, isFound_6_q, isFound_7_q,
       multiplexer_2_out;
  wire [2:0] adder_2_out, adder_3_out, i_q;
  wire [3:0] adder_1_out, adder_4_out, multiplexer_3_out, multiplexer_4_out, subtractor_1_out,
       subtractor_2_out;
  wire [3:3] i_q_2;
  wire [7:0] char_0_q, char_1_q, char_2_q, char_3_q, char_4_q, char_5_q, char_6_q, char_7_q, char_inputC_q,
       multiplexer_1_out;

  Register char_inputC (.D(I_inputC), .en(L_inputC), .Q(char_inputC_q), .clk(clk));  // open: clr
  Register char_0 (.D(I0), .en(L_chars), .Q(char_0_q), .clk(clk));  // open: clr
  Register char_1 (.D(I1), .en(L_chars), .Q(char_1_q), .clk(clk));  // open: clr
  Register char_2 (.D(I2), .en(L_chars), .Q(char_2_q), .clk(clk));  // open: clr
  Register char_3 (.D(I3), .en(L_chars), .Q(char_3_q), .clk(clk));  // open: clr
  Register char_4 (.D(I4), .en(L_chars), .Q(char_4_q), .clk(clk));  // open: clr
  Register char_5 (.D(I5), .en(L_chars), .Q(char_5_q), .clk(clk));  // open: clr
  Register char_6 (.D(I6), .en(L_chars), .Q(char_6_q), .clk(clk));  // open: clr
  Register char_7 (.D(I7), .en(L_chars), .Q(char_7_q), .clk(clk));  // open: clr
  Multiplexer #(.select(3), .width(8), .enable("false")) multiplexer_1 (
    .in0(char_0_q), .in1(char_1_q), .in2(char_2_q), .in3(char_3_q), .in4(char_4_q), .in5(char_5_q),
    .in6(char_6_q), .in7(char_7_q), .out(multiplexer_1_out), .sel(i_q));
  Comparator comparator_1 (.a(char_inputC_q), .b(multiplexer_1_out), .eq(word_i_eqInput));  // open: gt, lt
  Comparator comparator_2 (.a({8{1'b0}}), .b(multiplexer_1_out), .eq(word_i_eq0));  // open: gt, lt
  Multiplexer #(.enable("false")) multiplexer_2 (.in0(1'b0), .in1(1'b1), .out(multiplexer_2_out), .sel(S_found));
  Multiplexer #(.width(4), .enable("false")) multiplexer_3 (
    .in0(4'b1000), .in1(subtractor_1_out), .out(multiplexer_3_out), .sel(S_count_letters));
  Multiplexer #(.width(4), .enable("false")) multiplexer_4 (
    .in0(adder_4_out), .in1(subtractor_2_out), .out(multiplexer_4_out), .sel(S_i));
  Register #(.width(1)) u_found (.D(multiplexer_2_out), .en(L_found), .Q(found), .clk(clk));  // open: clr
  Register #(.width(4)) try (.D(adder_1_out), .en(L_try), .Q(Try_Count), .clk(clk), .clr(R_try));
  Register #(.width(4)) count_letters (
    .D(multiplexer_3_out), .en(L_count_letters), .Q(Letter_Count), .clk(clk));  // open: clr
  Register #(.width(4)) i (.D(multiplexer_4_out), .en(L_i), .Q({i_q_2[3], i_q}), .clk(clk), .clr(R_i));
  Register #(.width(3)) Player (.D(adder_2_out), .en(Player_Inc), .Q(Player_Count), .clk(clk), .clr(reset_count));
  Register #(.width(3)) Computer (.D(adder_3_out), .en(Comp_Inc), .Q(Computer_Count), .clk(clk), .clr(reset_count));
  Multiplexer #(.width(8), .enable("false")) multiplexer_5 (
    .in0(multiplexer_1_out), .in1(8'h5f), .out(TTY), .sel(S_char));
  Adder #(.width(4)) adder_1 (.a(4'b0001), .b(Try_Count), .out(adder_1_out));  // open: cin, cout
  Comparator #(.width(4), .mode("unsigned")) comparator_3 (.a(Try_Count), .b(4'b1010), .lt(try_lt10));  // open: gt, eq
  Adder #(.width(3)) adder_2 (.a(Player_Count), .b(3'b001), .out(adder_2_out));  // open: cin, cout
  Adder #(.width(3)) adder_3 (.a(Computer_Count), .b(3'b001), .out(adder_3_out));  // open: cin, cout
  Subtractor #(.width(4)) subtractor_1 (.a(Letter_Count), .b(4'b0001), .out(subtractor_1_out));  // open: bin, bout
  Subtractor #(.width(4)) subtractor_2 (.a(4'b1000), .b(Letter_Count), .out(subtractor_2_out));  // open: bin, bout
  Adder #(.width(4)) adder_4 (.a(4'b0001), .b({i_q_2[3], i_q}), .out(adder_4_out));  // open: cin, cout
  Comparator #(.width(4), .mode("unsigned")) comparator_4 (
    .a({i_q_2[3], i_q}), .b(4'b1000), .lt(i_lt8));  // open: gt, eq
  Demultiplexer #(.select(3), .enable("false")) demultiplexer_1 (
    .out0(demultiplexer_1_out0), .out1(demultiplexer_1_out1), .out2(demultiplexer_1_out2),
    .out3(demultiplexer_1_out3), .out4(demultiplexer_1_out4), .out5(demultiplexer_1_out5),
    .out6(demultiplexer_1_out6), .out7(demultiplexer_1_out7), .in(1'b1), .sel(i_q));
  and and_1 (and_1_out, demultiplexer_1_out0, L_isFound);
  and and_2 (and_2_out, demultiplexer_1_out1, L_isFound);
  and and_3 (and_3_out, demultiplexer_1_out2, L_isFound);
  and and_4 (and_4_out, demultiplexer_1_out3, L_isFound);
  and and_5 (and_5_out, demultiplexer_1_out4, L_isFound);
  and and_6 (and_6_out, demultiplexer_1_out5, L_isFound);
  and and_7 (and_7_out, demultiplexer_1_out6, L_isFound);
  and and_8 (and_8_out, demultiplexer_1_out7, L_isFound);
  Register #(.width(1)) isFound_0 (
    .D(demultiplexer_1_out0), .en(and_1_out), .Q(isFound_0_q), .clk(clk), .clr(R_isFound));
  Register #(.width(1)) isFound_1 (
    .D(demultiplexer_1_out1), .en(and_2_out), .Q(isFound_1_q), .clk(clk), .clr(R_isFound));
  Register #(.width(1)) isFound_2 (
    .D(demultiplexer_1_out2), .en(and_3_out), .Q(isFound_2_q), .clk(clk), .clr(R_isFound));
  Register #(.width(1)) isFound_3 (
    .D(demultiplexer_1_out3), .en(and_4_out), .Q(isFound_3_q), .clk(clk), .clr(R_isFound));
  Register #(.width(1)) isFound_4 (
    .D(demultiplexer_1_out4), .en(and_5_out), .Q(isFound_4_q), .clk(clk), .clr(R_isFound));
  Register #(.width(1)) isFound_5 (
    .D(demultiplexer_1_out5), .en(and_6_out), .Q(isFound_5_q), .clk(clk), .clr(R_isFound));
  Register #(.width(1)) isFound_6 (
    .D(demultiplexer_1_out6), .en(and_7_out), .Q(isFound_6_q), .clk(clk), .clr(R_isFound));
  Register #(.width(1)) isFound_7 (
    .D(demultiplexer_1_out7), .en(and_8_out), .Q(isFound_7_q), .clk(clk), .clr(R_isFound));
  Multiplexer #(.select(3), .enable("false")) multiplexer_6 (
    .in0(isFound_0_q), .in1(isFound_1_q), .in2(isFound_2_q), .in3(isFound_3_q), .in4(isFound_4_q),
    .in5(isFound_5_q), .in6(isFound_6_q), .in7(isFound_7_q), .out(isFound_i), .sel(i_q));
endmodule

module Hangman_ControlUnit (
  input  go,
  input  getInput,
  input  word_i_eqInput,
  input  found,
  input  word_i_eq0,
  input  isFound_i,
  input  try_lt10,
  input  i_lt8,
  input  clk,
  output L_inputC,
  output L_chars,
  output R_isFound,
  output L_isFound,
  output R_try,
  output L_try,
  output L_count_letters,
  output S_count_letters,
  output L_i,
  output S_i,
  output R_i,
  output L_found,
  output S_found,
  output Player_Inc,
  output Comp_inc,
  output S_char,
  output write,
  output R_TTY,
  output Display_7seg,
  output take_input,
  output [4:0] REGISTER
);

  wire not_1_out, not_2_out, not_3_out, not_4_out, not_5_out, not_6_out, not_7_out, not_8_out, not_9_out,
       not_10_out, not_11_out, not_12_out, not_13_out, not_14_out, not_15_out, not_16_out, not_17_out,
       not_18_out, not_19_out, not_20_out, not_21_out, not_22_out, not_23_out, not_24_out, not_25_out,
       not_26_out, not_27_out, not_28_out, not_29_out, not_30_out, not_31_out, not_32_out, not_33_out,
       not_34_out, not_35_out, not_36_out, not_37_out, not_38_out, not_39_out, not_40_out, not_41_out,
       not_42_out, not_43_out, not_44_out, not_45_out, not_46_out, not_47_out, not_48_out, not_49_out,
       not_50_out, not_51_out, not_52_out, not_53_out, not_54_out, not_55_out, not_56_out, not_57_out,
       not_58_out, not_59_out, not_60_out, not_61_out, not_62_out, not_63_out, not_64_out, not_65_out,
       S2_out, S4_out, S6_out, S9_out, S10_out, S12_out, S14_out, S15_out, S17_out, S18_out, S20_out,
       S21_out, S22_out, S25_out, S27_out, S28_out;
  wire [4:0] N0_n0;

  Register #(.width(5)) STATE_REG (.D(N0_n0), .Q(REGISTER), .clk(clk));  // open: en, clr
  N0 N0 (
    .S4(REGISTER[4]), .S3(REGISTER[3]), .S2(REGISTER[2]), .S1(REGISTER[1]), .S0(REGISTER[0]), .go(go),
    .getInput(getInput), .word_i_eqInput(word_i_eqInput), .found(found), .isFound_i(isFound_i),
    .try_lt10(try_lt10), .i_lt8(i_lt8), .N0(N0_n0[0]));
  N1 N1 (
    .S4(REGISTER[4]), .S3(REGISTER[3]), .S2(REGISTER[2]), .S1(REGISTER[1]), .S0(REGISTER[0]),
    .getInput(getInput), .word_eq0(word_i_eq0), .isFound_i(isFound_i), .try_lt10(try_lt10), .i_lt8(i_lt8),
    .N1(N0_n0[1]));
  N2 N2 (
    .S4(REGISTER[4]), .S3(REGISTER[3]), .S2(REGISTER[2]), .S1(REGISTER[1]), .S0(REGISTER[0]),
    .getInput(getInput), .word_i_eq0(word_i_eq0), .try_lt10(try_lt10), .i_lt8(i_lt8), .N2(N0_n0[2]));
  N3 N3 (
    .S4(REGISTER[4]), .S3(REGISTER[3]), .S2(REGISTER[2]), .S1(REGISTER[1]), .S0(REGISTER[0]),
    .try_lt10(try_lt10), .i_lt8(i_lt8), .N3(N0_n0[3]));
  N4 N4 (
    .S4(REGISTER[4]), .S3(REGISTER[3]), .S2(REGISTER[2]), .S1(REGISTER[1]), .S0(REGISTER[0]), .found(found),
    .try_lt10(try_lt10), .i_lt8(i_lt8), .N4(N0_n0[4]));
  not not_1 (not_1_out, REGISTER[4]);
  not not_2 (not_2_out, REGISTER[3]);
  not not_3 (not_3_out, REGISTER[2]);
  not not_4 (not_4_out, REGISTER[1]);
  not not_5 (not_5_out, REGISTER[4]);
  not not_6 (not_6_out, REGISTER[3]);
  not not_7 (not_7_out, REGISTER[2]);
  not not_8 (not_8_out, REGISTER[0]);
  not not_9 (not_9_out, REGISTER[4]);
  not not_10 (not_10_out, REGISTER[3]);
  not not_11 (not_11_out, REGISTER[2]);
  not not_12 (not_12_out, REGISTER[4]);
  not not_13 (not_13_out, REGISTER[3]);
  not not_14 (not_14_out, REGISTER[1]);
  not not_15 (not_15_out, REGISTER[0]);
  not not_16 (not_16_out, REGISTER[4]);
  not not_17 (not_17_out, REGISTER[3]);
  not not_18 (not_18_out, REGISTER[1]);
  not not_19 (not_19_out, REGISTER[4]);
  not not_20 (not_20_out, REGISTER[3]);
  not not_21 (not_21_out, REGISTER[0]);
  not not_22 (not_22_out, REGISTER[4]);
  not not_23 (not_23_out, REGISTER[2]);
  not not_24 (not_24_out, REGISTER[1]);
  not not_25 (not_25_out, REGISTER[0]);
  not not_26 (not_26_out, REGISTER[4]);
  not not_27 (not_27_out, REGISTER[2]);
  not not_28 (not_28_out, REGISTER[1]);
  not not_29 (not_29_out, REGISTER[4]);
  not not_30 (not_30_out, REGISTER[2]);
  not not_31 (not_31_out, REGISTER[0]);
  not not_32 (not_32_out, REGISTER[4]);
  not not_33 (not_33_out, REGISTER[2]);
  not not_34 (not_34_out, REGISTER[4]);
  not not_35 (not_35_out, REGISTER[1]);
  not not_36 (not_36_out, REGISTER[0]);
  not not_37 (not_37_out, REGISTER[4]);
  not not_38 (not_38_out, REGISTER[0]);
  not not_39 (not_39_out, REGISTER[4]);
  not not_40 (not_40_out, REGISTER[3]);
  not not_41 (not_41_out, REGISTER[2]);
  not not_42 (not_42_out, REGISTER[1]);
  not not_43 (not_43_out, REGISTER[0]);
  not not_44 (not_44_out, REGISTER[3]);
  not not_45 (not_45_out, REGISTER[2]);
  not not_46 (not_46_out, REGISTER[1]);
  not not_47 (not_47_out, REGISTER[3]);
  not not_48 (not_48_out, REGISTER[2]);
  not not_49 (not_49_out, REGISTER[0]);
  not not_50 (not_50_out, REGISTER[3]);
  not not_51 (not_51_out, REGISTER[1]);
  not not_52 (not_52_out, REGISTER[0]);
  not not_53 (not_53_out, REGISTER[3]);
  not not_54 (not_54_out, REGISTER[1]);
  not not_55 (not_55_out, REGISTER[3]);
  not not_56 (not_56_out, REGISTER[0]);
  not not_57 (not_57_out, REGISTER[3]);
  not not_58 (not_58_out, REGISTER[2]);
  not not_59 (not_59_out, REGISTER[1]);
  not not_60 (not_60_out, REGISTER[0]);
  not not_61 (not_61_out, REGISTER[2]);
  not not_62 (not_62_out, REGISTER[1]);
  not not_63 (not_63_out, REGISTER[2]);
  not not_64 (not_64_out, REGISTER[1]);
  not not_65 (not_65_out, REGISTER[0]);
  and S1 (L_chars, not_1_out, not_2_out, not_3_out, not_4_out, REGISTER[0]);
  and S2 (S2_out, not_5_out, not_6_out, not_7_out, REGISTER[1], not_8_out);
  and S3 (S_count_letters, not_9_out, not_10_out, not_11_out, REGISTER[1], REGISTER[0]);
  and S4 (S4_out, not_12_out, not_13_out, REGISTER[2], not_14_out, not_15_out);
  and S5 (Display_7seg, not_16_out, not_17_out, REGISTER[2], not_18_out, REGISTER[0]);
  and S6 (S6_out, not_19_out, not_20_out, REGISTER[2], REGISTER[1], not_21_out);
  and S8 (S_char, not_22_out, REGISTER[3], not_23_out, not_24_out, not_25_out);
  and S9 (S9_out, not_26_out, REGISTER[3], not_27_out, not_28_out, REGISTER[0]);
  and S10 (S10_out, not_29_out, REGISTER[3], not_30_out, REGISTER[1], not_31_out);
  and S11 (L_inputC, not_32_out, REGISTER[3], not_33_out, REGISTER[1], REGISTER[0]);
  and S12 (S12_out, not_34_out, REGISTER[3], REGISTER[2], not_35_out, not_36_out);
  and S14 (S14_out, not_37_out, REGISTER[3], REGISTER[2], REGISTER[1], not_38_out);
  and S15 (S15_out, not_39_out, REGISTER[3], REGISTER[2], REGISTER[1], REGISTER[0]);
  and S16 (L_try, REGISTER[4], not_40_out, not_41_out, not_42_out, not_43_out);
  and S17 (S17_out, REGISTER[4], not_44_out, not_45_out, not_46_out, REGISTER[0]);
  and S18 (S18_out, REGISTER[4], not_47_out, not_48_out, REGISTER[1], not_49_out);
  and S20 (S20_out, REGISTER[4], not_50_out, REGISTER[2], not_51_out, not_52_out);
  and S21 (S21_out, REGISTER[4], not_53_out, REGISTER[2], not_54_out, REGISTER[0]);
  and S22 (S22_out, REGISTER[4], not_55_out, REGISTER[2], REGISTER[1], not_56_out);
  and S23 (Player_Inc, REGISTER[4], not_57_out, REGISTER[2], REGISTER[1], REGISTER[0]);
  and S24 (Comp_inc, REGISTER[4], REGISTER[3], not_58_out, not_59_out, not_60_out);
  and S25 (S25_out, REGISTER[4], REGISTER[3], not_61_out, not_62_out, REGISTER[0]);
  and S27 (S27_out, REGISTER[4], REGISTER[3], not_63_out, REGISTER[1], REGISTER[0]);
  and S28 (S28_out, REGISTER[4], REGISTER[3], REGISTER[2], not_64_out, not_65_out);
  or or_1 (L_isFound, S_count_letters, S14_out);
  or or_2 (L_count_letters, L_chars, S_count_letters);
  or or_3 (L_i, S4_out, S6_out, S9_out, S12_out, S15_out, S21_out, S25_out, S28_out);
  or or_4 (S_i, S6_out, S12_out, S25_out);
  or or_5 (R_i, S2_out, S18_out);
  or or_6 (L_found, L_inputC, S14_out, S17_out, S20_out);
  or or_7 (S_found, S14_out, S17_out);
  or or_8 (write, S_char, S27_out, S10_out);
  or or_9 (R_TTY, L_chars, S22_out);

  assign R_isFound = L_chars;
  assign R_try = L_chars;
  assign take_input = L_inputC;
endmodule

module _7SegmentDisplay (
  input  [3:0] State,
  input  Load,
  input  Reset,
  input  clk,
  output M,
  output UL,
  output U,
  output UR,
  output BR,
  output B,
  output BL
);

  wire not_1_out, not_2_out, not_3_out, not_4_out, not_5_out, not_6_out, not_7_out, not_8_out, not_9_out,
       not_10_out, not_11_out, not_12_out, not_13_out, not_14_out, not_15_out, not_16_out, not_17_out,
       not_18_out, not_19_out, not_20_out, not_21_out, not_22_out, not_23_out, not_24_out, not_25_out,
       not_26_out, not_27_out, or_3_out, or_4_out, or_5_out, s0_out, s1_out, s2_out, s3_out, s4_out, s5_out,
       s6_out, s7_out, s8_out, s9_out, s10_out;
  wire [3:0] state_q;

  Register #(.width(4)) u_state (.D(State), .en(Load), .Q(state_q), .clk(clk), .clr(Reset));
  not not_1 (not_1_out, state_q[3]);
  not not_2 (not_2_out, state_q[2]);
  and s0 (s0_out, not_1_out, not_2_out, not_3_out, not_4_out);
  not not_3 (not_3_out, state_q[1]);
  not not_4 (not_4_out, state_q[0]);
  not not_5 (not_5_out, state_q[3]);
  not not_6 (not_6_out, state_q[2]);
  and s1 (s1_out, not_5_out, not_6_out, not_7_out, state_q[0]);
  not not_7 (not_7_out, state_q[1]);
  not not_8 (not_8_out, state_q[3]);
  not not_9 (not_9_out, state_q[2]);
  and s2 (s2_out, not_8_out, not_9_out, state_q[1], not_10_out);
  not not_10 (not_10_out, state_q[0]);
  not not_11 (not_11_out, state_q[3]);
  not not_12 (not_12_out, state_q[2]);
  and s3 (s3_out, not_11_out, not_12_out, state_q[1], state_q[0]);
  not not_13 (not_13_out, state_q[3]);
  and s4 (s4_out, not_13_out, state_q[2], not_14_out, not_15_out);
  not not_14 (not_14_out, state_q[1]);
  not not_15 (not_15_out, state_q[0]);
  not not_16 (not_16_out, state_q[3]);
  and s5 (s5_out, not_16_out, state_q[2], not_17_out, state_q[0]);
  not not_17 (not_17_out, state_q[1]);
  not not_18 (not_18_out, state_q[3]);
  and s6 (s6_out, not_18_out, state_q[2], state_q[1], not_19_out);
  not not_19 (not_19_out, state_q[0]);
  not not_20 (not_20_out, state_q[3]);
  and s7 (s7_out, not_20_out, state_q[2], state_q[1], state_q[0]);
  not not_21 (not_21_out, state_q[2]);
  and s8 (s8_out, state_q[3], not_21_out, not_22_out, not_23_out);
  not not_22 (not_22_out, state_q[1]);
  not not_23 (not_23_out, state_q[0]);
  not not_24 (not_24_out, state_q[2]);
  and s9 (s9_out, state_q[3], not_24_out, not_25_out, state_q[0]);
  not not_25 (not_25_out, state_q[1]);
  not not_26 (not_26_out, state_q[2]);
  and s10 (s10_out, state_q[3], not_26_out, state_q[1], not_27_out);
  not not_27 (not_27_out, state_q[0]);
  or or_1 (M, s2_out, s3_out, s4_out, s5_out, s6_out, s8_out, s9_out);
  or or_2 (UL, s0_out, s4_out, s5_out, s6_out, s8_out, s9_out, s10_out);
  not not_28 (U, or_3_out);
  or or_3 (or_3_out, s1_out, s4_out);
  or or_4 (or_4_out, s5_out, s6_out);
  not not_29 (UR, or_4_out);
  not not_30 (BR, s2_out);
  not not_31 (B, or_5_out);
  or or_5 (or_5_out, s1_out, s4_out, s7_out);
  or or_6 (BL, s0_out, s2_out, s6_out, s8_out, s10_out);
endmodule

module MyKeyboard (
  input  take_input,
  input  a,
  input  b,
  input  c,
  input  d,
  input  e,
  input  f,
  input  g,
  input  h,
  input  i,
  input  j,
  input  k,
  input  l,
  input  m,
  input  n,
  input  o,
  input  p,
  input  q,
  input  r,
  input  s,
  input  t,
  input  u,
  input  v,
  input  w,
  input  x,
  input  y,
  input  z,
  output [6:0] I_Guess,
  output getInput
);

  wire [6:0] multiplexer_1_out, multiplexer_2_out, multiplexer_3_out, multiplexer_4_out, multiplexer_5_out,
       multiplexer_6_out, multiplexer_7_out, multiplexer_8_out, multiplexer_9_out, multiplexer_10_out,
       multiplexer_11_out, multiplexer_13_out, multiplexer_14_out, multiplexer_15_out, multiplexer_16_out,
       multiplexer_17_out, multiplexer_18_out, multiplexer_19_out, multiplexer_20_out, multiplexer_21_out,
       multiplexer_22_out, multiplexer_23_out, multiplexer_24_out, multiplexer_25_out, multiplexer_26_out,
       multiplexer_27_out, or_2_out;

  Multiplexer #(.width(7), .enable("false")) multiplexer_1 (
    .in0({7{1'b0}}), .in1(7'b1100001), .out(multiplexer_1_out), .sel(a));
  Multiplexer #(.width(7), .enable("false")) multiplexer_2 (
    .in0({7{1'b0}}), .in1(7'b1100010), .out(multiplexer_2_out), .sel(b));
  Multiplexer #(.width(7), .enable("false")) multiplexer_3 (
    .in0({7{1'b0}}), .in1(7'b1100011), .out(multiplexer_3_out), .sel(c));
  Multiplexer #(.width(7), .enable("false")) multiplexer_4 (
    .in0({7{1'b0}}), .in1(7'b1100101), .out(multiplexer_4_out), .sel(e));
  Multiplexer #(.width(7), .enable("false")) multiplexer_5 (
    .in0({7{1'b0}}), .in1(7'b1100100), .out(multiplexer_5_out), .sel(d));
  Multiplexer #(.width(7), .enable("false")) multiplexer_6 (
    .in0({7{1'b0}}), .in1(7'b1100111), .out(multiplexer_6_out), .sel(g));
  Multiplexer #(.width(7), .enable("false")) multiplexer_7 (
    .in0({7{1'b0}}), .in1(7'b1100110), .out(multiplexer_7_out), .sel(f));
  Multiplexer #(.width(7), .enable("false")) multiplexer_8 (
    .in0({7{1'b0}}), .in1(7'b1101000), .out(multiplexer_8_out), .sel(h));
  Multiplexer #(.width(7), .enable("false")) multiplexer_9 (
    .in0({7{1'b0}}), .in1(7'b1101010), .out(multiplexer_9_out), .sel(j));
  Multiplexer #(.width(7), .enable("false")) multiplexer_10 (
    .in0({7{1'b0}}), .in1(7'b1101001), .out(multiplexer_10_out), .sel(i));
  Multiplexer #(.width(7), .enable("false")) multiplexer_11 (
    .in0({7{1'b0}}), .in1(7'b1101011), .out(multiplexer_11_out), .sel(k));
  Multiplexer #(.width(7), .enable("false")) multiplexer_12 (
    .in0({7{1'b0}}), .in1(or_2_out), .out(I_Guess), .sel(take_input));
  Multiplexer #(.width(7), .enable("false")) multiplexer_13 (
    .in0({7{1'b0}}), .in1(7'b1101101), .out(multiplexer_13_out), .sel(m));
  Multiplexer #(.width(7), .enable("false")) multiplexer_14 (
    .in0({7{1'b0}}), .in1(7'b1101100), .out(multiplexer_14_out), .sel(l));
  or or_1 (getInput, a, b, c, d, e, f, g, h, i, j, k, l, m, n, o, p, q, r, s, t, u, v, w, x, y, z);
  assign or_2_out = multiplexer_1_out | multiplexer_2_out | multiplexer_3_out | multiplexer_5_out | multiplexer_4_out | multiplexer_7_out | multiplexer_6_out | multiplexer_8_out | multiplexer_10_out | multiplexer_9_out | multiplexer_11_out | multiplexer_14_out | multiplexer_13_out | multiplexer_16_out | multiplexer_15_out | multiplexer_17_out | multiplexer_18_out | multiplexer_19_out | multiplexer_20_out | multiplexer_21_out | multiplexer_22_out | multiplexer_24_out | multiplexer_23_out | multiplexer_25_out | multiplexer_26_out | multiplexer_27_out;  // OR_Gate or_2, 7 bits wide
  Multiplexer #(.width(7), .enable("false")) multiplexer_15 (
    .in0({7{1'b0}}), .in1(7'b1101111), .out(multiplexer_15_out), .sel(o));
  Multiplexer #(.width(7), .enable("false")) multiplexer_16 (
    .in0({7{1'b0}}), .in1(7'b1101110), .out(multiplexer_16_out), .sel(n));
  Multiplexer #(.width(7), .enable("false")) multiplexer_17 (
    .in0({7{1'b0}}), .in1(7'b1110000), .out(multiplexer_17_out), .sel(p));
  Multiplexer #(.width(7), .enable("false")) multiplexer_18 (
    .in0({7{1'b0}}), .in1(7'b1110001), .out(multiplexer_18_out), .sel(q));
  Multiplexer #(.width(7), .enable("false")) multiplexer_19 (
    .in0({7{1'b0}}), .in1(7'b1110010), .out(multiplexer_19_out), .sel(r));
  Multiplexer #(.width(7), .enable("false")) multiplexer_20 (
    .in0({7{1'b0}}), .in1(7'b1110011), .out(multiplexer_20_out), .sel(s));
  Multiplexer #(.width(7), .enable("false")) multiplexer_21 (
    .in0({7{1'b0}}), .in1(7'b1110100), .out(multiplexer_21_out), .sel(t));
  Multiplexer #(.width(7), .enable("false")) multiplexer_22 (
    .in0({7{1'b0}}), .in1(7'b1110101), .out(multiplexer_22_out), .sel(u));
  Multiplexer #(.width(7), .enable("false")) multiplexer_23 (
    .in0({7{1'b0}}), .in1(7'b1110111), .out(multiplexer_23_out), .sel(w));
  Multiplexer #(.width(7), .enable("false")) multiplexer_24 (
    .in0({7{1'b0}}), .in1(7'b1110110), .out(multiplexer_24_out), .sel(v));
  Multiplexer #(.width(7), .enable("false")) multiplexer_25 (
    .in0({7{1'b0}}), .in1(7'b1111000), .out(multiplexer_25_out), .sel(x));
  Multiplexer #(.width(7), .enable("false")) multiplexer_26 (
    .in0({7{1'b0}}), .in1(7'b1111001), .out(multiplexer_26_out), .sel(y));
  Multiplexer #(.width(7), .enable("false")) multiplexer_27 (
    .in0({7{1'b0}}), .in1(7'b1111001), .out(multiplexer_27_out), .sel(z));
endmodule

module LedMatrix (
  input  [3:0] Input,
  output [6:0] O0,
  output [6:0] O1,
  output [6:0] O2,
  output [6:0] O3,
  output [6:0] O4
);

  wire comparator_1_gt, comparator_2_gt, comparator_3_gt, comparator_4_gt, comparator_5_gt, comparator_6_gt,
       comparator_7_gt, comparator_8_gt, comparator_9_gt, comparator_10_gt;
  wire [6:0] multiplexer_3_out, multiplexer_4_out, multiplexer_5_out, multiplexer_6_out, multiplexer_7_out,
       multiplexer_10_out;

  Comparator #(.width(4), .mode("unsigned")) comparator_1 (
    .a(Input), .b(4'b0000), .gt(comparator_1_gt));  // open: eq, lt
  Comparator #(.width(4), .mode("unsigned")) comparator_2 (
    .a(Input), .b(4'b0001), .gt(comparator_2_gt));  // open: eq, lt
  Comparator #(.width(4), .mode("unsigned")) comparator_3 (
    .a(Input), .b(4'b0010), .gt(comparator_3_gt));  // open: eq, lt
  Comparator #(.width(4), .mode("unsigned")) comparator_4 (
    .a(Input), .b(4'b0011), .gt(comparator_4_gt));  // open: eq, lt
  Comparator #(.width(4), .mode("unsigned")) comparator_5 (
    .a(Input), .b(4'b0100), .gt(comparator_5_gt));  // open: eq, lt
  Comparator #(.width(4), .mode("unsigned")) comparator_6 (
    .a(Input), .b(4'b0101), .gt(comparator_6_gt));  // open: eq, lt
  Comparator #(.width(4), .mode("unsigned")) comparator_7 (
    .a(Input), .b(4'b0110), .gt(comparator_7_gt));  // open: eq, lt
  Comparator #(.width(4), .mode("unsigned")) comparator_8 (
    .a(Input), .b(4'b0111), .gt(comparator_8_gt));  // open: eq, lt
  Comparator #(.width(4), .mode("unsigned")) comparator_9 (
    .a(Input), .b(4'b1000), .gt(comparator_9_gt));  // open: eq, lt
  Comparator #(.width(4), .mode("unsigned")) comparator_10 (
    .a(Input), .b(4'b1001), .gt(comparator_10_gt));  // open: eq, lt
  Multiplexer #(.width(7), .enable("false")) multiplexer_1 (
    .in0({7{1'b0}}), .in1({7{1'b1}}), .out(O0), .sel(comparator_1_gt));
  Multiplexer #(.width(7), .enable("false")) multiplexer_2 (
    .in0({7{1'b0}}), .in1(7'b1000000), .out(O1), .sel(comparator_2_gt));
  Multiplexer #(.width(7), .enable("false")) multiplexer_3 (
    .in0({7{1'b0}}), .in1(7'b1000000), .out(multiplexer_3_out), .sel(comparator_2_gt));
  Multiplexer #(.width(7), .enable("false")) multiplexer_4 (
    .in0(multiplexer_3_out), .in1(7'b1010000), .out(multiplexer_4_out), .sel(comparator_5_gt));
  Multiplexer #(.width(7), .enable("false")) multiplexer_5 (
    .in0({7{1'b0}}), .in1(7'b0100000), .out(multiplexer_5_out), .sel(comparator_3_gt));
  Multiplexer #(.width(7), .enable("false")) multiplexer_6 (
    .in0(multiplexer_5_out), .in1(7'b0110000), .out(multiplexer_6_out), .sel(comparator_4_gt));
  Multiplexer #(.width(7), .enable("false")) multiplexer_7 (
    .in0({7{1'b0}}), .in1(7'b0010000), .out(multiplexer_7_out), .sel(comparator_6_gt));
  Multiplexer #(.width(7), .enable("false")) multiplexer_8 (
    .in0(multiplexer_7_out), .in1(7'b0010010), .out(O4), .sel(comparator_10_gt));
  Multiplexer #(.width(7), .enable("false")) multiplexer_9 (
    .in0(multiplexer_4_out), .in1(7'b1010010), .out(O2), .sel(comparator_9_gt));
  Multiplexer #(.width(7), .enable("false")) multiplexer_10 (
    .in0(multiplexer_6_out), .in1(7'b0111000), .out(multiplexer_10_out), .sel(comparator_7_gt));
  Multiplexer #(.width(7), .enable("false")) multiplexer_11 (
    .in0(multiplexer_10_out), .in1(7'b0111100), .out(O3), .sel(comparator_8_gt));
endmodule

module N0 (
  input  S4,
  input  S3,
  input  S2,
  input  S1,
  input  S0,
  input  go,
  input  getInput,
  input  word_i_eqInput,
  input  found,
  input  isFound_i,
  input  try_lt10,
  input  i_lt8,
  output N0
);

  wire and_1_out, and_2_out, and_3_out, and_4_out, and_5_out, and_6_out, and_7_out, and_8_out, and_9_out,
       and_10_out, and_11_out, and_12_out, and_13_out, and_14_out, and_15_out, and_16_out, and_17_out,
       and_18_out, and_19_out, and_20_out, and_21_out, and_22_out, not_1_out, not_2_out, not_3_out,
       not_4_out, not_5_out, not_6_out, not_7_out, not_8_out, not_9_out, not_10_out, not_11_out, not_12_out,
       not_13_out, not_14_out, not_15_out, not_16_out, not_17_out, not_18_out, not_19_out, not_20_out,
       not_21_out, not_22_out, not_23_out, not_24_out, not_25_out, not_26_out, not_27_out, not_28_out,
       not_29_out, not_30_out, not_31_out, not_32_out, not_33_out, not_34_out, not_35_out, not_36_out,
       not_37_out, not_38_out, not_39_out, not_40_out, not_41_out, not_42_out, not_43_out, not_44_out,
       not_45_out, not_46_out, not_47_out, not_48_out, not_49_out, not_50_out, not_51_out, not_52_out,
       not_53_out, not_54_out, not_55_out, not_56_out, or_1_out, or_2_out, or_3_out;

  not not_1 (not_1_out, S4);
  not not_2 (not_2_out, S3);
  not not_3 (not_3_out, S2);
  not not_4 (not_4_out, S1);
  not not_5 (not_5_out, S0);
  not not_6 (not_6_out, S4);
  not not_7 (not_7_out, S3);
  not not_8 (not_8_out, S2);
  not not_9 (not_9_out, S0);
  not not_10 (not_10_out, S4);
  not not_11 (not_11_out, S3);
  not not_12 (not_12_out, S0);
  not not_13 (not_13_out, S4);
  not not_14 (not_14_out, S3);
  not not_15 (not_15_out, i_lt8);
  not not_16 (not_16_out, S4);
  not not_17 (not_17_out, S2);
  not not_18 (not_18_out, S1);
  not not_19 (not_19_out, S4);
  not not_20 (not_20_out, S2);
  not not_21 (not_21_out, S0);
  not not_22 (not_22_out, S4);
  not not_23 (not_23_out, S2);
  not not_24 (not_24_out, getInput);
  not not_25 (not_25_out, S4);
  not not_26 (not_26_out, S1);
  not not_27 (not_27_out, S0);
  not not_28 (not_28_out, word_i_eqInput);
  or or_1 (or_1_out, not_28_out, isFound_i);
  and and_1 (and_1_out, found, not_29_out);
  not not_29 (not_29_out, i_lt8);
  not not_30 (not_30_out, S4);
  not not_31 (not_31_out, S1);
  not not_32 (not_32_out, S4);
  not not_33 (not_33_out, S3);
  not not_34 (not_34_out, S2);
  not not_35 (not_35_out, S1);
  not not_36 (not_36_out, S0);
  not not_37 (not_37_out, S3);
  not not_38 (not_38_out, S2);
  not not_39 (not_39_out, S0);
  not not_40 (not_40_out, S3);
  not not_41 (not_41_out, S2);
  not not_42 (not_42_out, S3);
  not not_43 (not_43_out, S1);
  not not_44 (not_44_out, S3);
  not not_45 (not_45_out, S0);
  not not_46 (not_46_out, S3);
  not not_47 (not_47_out, S2);
  not not_48 (not_48_out, S1);
  not not_49 (not_49_out, S0);
  not not_50 (not_50_out, S2);
  not not_51 (not_51_out, S0);
  not not_52 (not_52_out, S1);
  not not_53 (not_53_out, S4);
  not not_54 (not_54_out, S3);
  not not_55 (not_55_out, S1);
  not not_56 (not_56_out, S0);
  and and_2 (and_2_out, not_1_out, not_2_out, not_3_out, not_4_out, not_5_out, go);
  and and_3 (and_3_out, not_6_out, not_7_out, not_8_out, S1, not_9_out);
  and and_4 (and_4_out, not_10_out, not_11_out, S2, S1, not_12_out, try_lt10);
  and and_5 (and_5_out, not_13_out, not_14_out, S2, S1, S0, not_15_out);
  and and_6 (and_6_out, not_16_out, S3, not_17_out, not_18_out);
  and and_7 (and_7_out, not_19_out, S3, not_20_out, S1, not_21_out);
  and and_8 (and_8_out, not_22_out, S3, not_23_out, S1, S0, not_24_out);
  and and_9 (and_9_out, not_25_out, S3, S2, not_26_out, not_27_out);
  and and_10 (and_10_out, or_1_out, i_lt8);
  and and_11 (and_11_out, not_30_out, S3, S2, not_31_out, S0, or_2_out);
  and and_12 (and_12_out, not_32_out, S3, S2, S1);
  and and_13 (and_13_out, S4, not_33_out, not_34_out, not_35_out, not_36_out);
  and and_14 (and_14_out, S4, not_37_out, not_38_out, S1, not_39_out);
  and and_15 (and_15_out, S4, not_40_out, not_41_out, S1, S0, isFound_i, i_lt8);
  and and_16 (and_16_out, S4, not_42_out, S2, not_43_out);
  and and_17 (and_17_out, S4, not_44_out, S2, S1, not_45_out, found);
  and and_18 (and_18_out, S4, not_46_out, S2, S1, S0);
  and and_19 (and_19_out, S4, S3, not_47_out, not_48_out, not_49_out);
  and and_20 (and_20_out, S4, S3, not_50_out, S1, not_51_out, i_lt8);
  and and_21 (and_21_out, S4, S3, S0, S2, not_52_out);
  and and_22 (and_22_out, not_53_out, not_54_out, S2, not_55_out, not_56_out);
  or or_2 (or_2_out, and_10_out, and_1_out);
  or or_3 (or_3_out, and_21_out, and_22_out);
  or or_4 (N0, and_2_out, and_3_out, and_4_out, and_5_out, and_6_out, and_7_out, and_8_out, and_9_out, and_11_out, and_12_out, and_13_out, and_14_out, and_15_out, and_16_out, and_17_out, and_18_out, and_19_out, and_20_out, or_3_out);
endmodule

module N1 (
  input  S4,
  input  S3,
  input  S2,
  input  S1,
  input  S0,
  input  getInput,
  input  word_eq0,
  input  isFound_i,
  input  try_lt10,
  input  i_lt8,
  output N1
);

  wire and_1_out, and_2_out, and_3_out, and_4_out, and_5_out, and_6_out, and_7_out, and_8_out, and_9_out,
       and_10_out, and_11_out, and_12_out, and_13_out, and_14_out, and_15_out, and_16_out, not_1_out,
       not_2_out, not_3_out, not_4_out, not_5_out, not_6_out, not_7_out, not_8_out, not_9_out, not_10_out,
       not_11_out, not_12_out, not_13_out, not_14_out, not_15_out, not_16_out, not_17_out, not_18_out,
       not_19_out, not_20_out, not_21_out, not_22_out, not_23_out, not_24_out, not_25_out, not_26_out,
       not_27_out, not_28_out, not_29_out, not_30_out, not_31_out, not_32_out, not_33_out, not_34_out,
       not_35_out, not_36_out, not_37_out, or_1_out, xor_1_out, xor_2_out;

  not not_1 (not_1_out, isFound_i);
  not not_2 (not_2_out, S4);
  not not_3 (not_3_out, S3);
  not not_4 (not_4_out, S2);
  not not_5 (not_5_out, S1);
  not not_6 (not_6_out, S1);
  not not_7 (not_7_out, S4);
  not not_8 (not_8_out, S3);
  not not_9 (not_9_out, S1);
  not not_10 (not_10_out, S4);
  not not_11 (not_11_out, S3);
  not not_12 (not_12_out, S0);
  not not_13 (not_13_out, S4);
  not not_14 (not_14_out, S3);
  not not_15 (not_15_out, and_1_out);
  and and_1 (and_1_out, not_1_out, i_lt8);
  not not_16 (not_16_out, S4);
  not not_17 (not_17_out, S2);
  not not_18 (not_18_out, S1);
  not not_19 (not_19_out, S4);
  not not_20 (not_20_out, S2);
  not not_21 (not_21_out, getInput);
  not not_22 (not_22_out, S4);
  not not_23 (not_23_out, S1);
  not not_24 (not_24_out, S4);
  not not_25 (not_25_out, S0);
  not not_26 (not_26_out, S3);
  not not_27 (not_27_out, S2);
  xor xor_1 (xor_1_out, S1, S0);
  not not_28 (not_28_out, S3);
  not not_29 (not_29_out, S2);
  not not_30 (not_30_out, i_lt8);
  not not_31 (not_31_out, S3);
  xor xor_2 (xor_2_out, S1, S0);
  not not_32 (not_32_out, S2);
  not not_33 (not_33_out, S1);
  not not_34 (not_34_out, S2);
  not not_35 (not_35_out, S0);
  not not_36 (not_36_out, S1);
  not not_37 (not_37_out, S0);
  and and_2 (and_2_out, not_2_out, not_3_out, not_4_out, not_5_out, S0);
  and and_3 (and_3_out, S4, S3, S2, not_6_out, S0, word_eq0, i_lt8);
  and and_4 (and_4_out, not_7_out, not_8_out, S0, S2, not_9_out);
  and and_5 (and_5_out, not_10_out, not_11_out, S2, S1, not_12_out, try_lt10);
  and and_6 (and_6_out, not_13_out, not_14_out, S2, S1, S0, not_15_out);
  and and_7 (and_7_out, not_16_out, S3, not_17_out, not_18_out, S0);
  and and_8 (and_8_out, not_19_out, S3, not_20_out, S1, S0, not_21_out);
  and and_9 (and_9_out, not_22_out, S3, S2, not_23_out, S0, i_lt8);
  and and_10 (and_10_out, not_24_out, S3, S2, S1, not_25_out);
  and and_11 (and_11_out, S4, not_26_out, not_27_out, xor_1_out);
  and and_12 (and_12_out, S4, not_28_out, not_29_out, S1, S0, not_30_out);
  and and_13 (and_13_out, S4, not_31_out, S2, xor_2_out);
  and and_14 (and_14_out, S4, S3, not_32_out, not_33_out, S0);
  and and_15 (and_15_out, S4, S3, not_34_out, S1, not_35_out, i_lt8);
  and and_16 (and_16_out, S4, S3, S2, not_36_out, not_37_out);
  or or_1 (or_1_out, and_15_out, and_16_out);
  or or_2 (N1, and_2_out, and_3_out, and_4_out, and_5_out, and_6_out, and_7_out, and_8_out, and_9_out, and_10_out, and_11_out, and_12_out, and_13_out, and_14_out, or_1_out);
endmodule

module N2 (
  input  S4,
  input  S3,
  input  S2,
  input  S1,
  input  S0,
  input  getInput,
  input  word_i_eq0,
  input  try_lt10,
  input  i_lt8,
  output N2
);

  wire and_1_out, and_2_out, and_3_out, and_4_out, and_5_out, and_6_out, and_7_out, and_8_out, and_9_out,
       and_10_out, and_11_out, and_12_out, and_13_out, not_1_out, not_2_out, not_3_out, not_4_out, not_5_out,
       not_6_out, not_7_out, not_8_out, not_9_out, not_10_out, not_11_out, not_12_out, not_13_out,
       not_14_out, not_15_out, not_16_out, not_17_out, not_18_out, not_19_out, not_20_out, not_21_out,
       not_22_out, not_23_out, not_24_out, not_25_out, not_26_out, not_27_out, not_28_out, not_29_out,
       not_30_out, not_31_out, not_32_out, not_33_out, not_34_out, or_1_out, or_2_out, or_3_out;

  not not_1 (not_1_out, word_i_eq0);
  not not_2 (not_2_out, i_lt8);
  not not_3 (not_3_out, S4);
  not not_4 (not_4_out, S3);
  not not_5 (not_5_out, S2);
  not not_6 (not_6_out, S0);
  not not_7 (not_7_out, S4);
  not not_8 (not_8_out, S3);
  not not_9 (not_9_out, S1);
  not not_10 (not_10_out, S0);
  not not_11 (not_11_out, S4);
  not not_12 (not_12_out, S3);
  not not_13 (not_13_out, S2);
  not not_14 (not_14_out, S4);
  not not_15 (not_15_out, S3);
  not not_16 (not_16_out, S1);
  not not_17 (not_17_out, S4);
  not not_18 (not_18_out, S3);
  not not_19 (not_19_out, S0);
  not not_20 (not_20_out, S4);
  not not_21 (not_21_out, S2);
  not not_22 (not_22_out, S1);
  not not_23 (not_23_out, S4);
  not not_24 (not_24_out, S2);
  not not_25 (not_25_out, S4);
  not not_26 (not_26_out, S1);
  not not_27 (not_27_out, S0);
  not not_28 (not_28_out, S4);
  not not_29 (not_29_out, S1);
  not not_30 (not_30_out, S4);
  not not_31 (not_31_out, S2);
  not not_32 (not_32_out, S3);
  not not_33 (not_33_out, S0);
  not not_34 (not_34_out, S1);
  or or_1 (or_1_out, not_1_out, not_2_out);
  and and_1 (and_1_out, not_3_out, not_4_out, not_5_out, S1, not_6_out);
  and and_2 (and_2_out, not_7_out, not_8_out, S2, not_9_out, not_10_out);
  and and_3 (and_3_out, not_11_out, not_12_out, not_13_out, S1, S0);
  and and_4 (and_4_out, not_14_out, not_15_out, S2, not_16_out, S0);
  and and_5 (and_5_out, not_17_out, not_18_out, S2, S1, not_19_out, try_lt10);
  and and_6 (and_6_out, not_20_out, S3, not_21_out, not_22_out, S0);
  and and_7 (and_7_out, not_23_out, S3, not_24_out, S1, S0, getInput);
  and and_8 (and_8_out, not_25_out, S3, S2, not_26_out, not_27_out);
  and and_9 (and_9_out, not_28_out, S3, S2, not_29_out, S0, i_lt8);
  and and_10 (and_10_out, not_30_out, S3, S2, S1);
  and and_11 (and_11_out, S4, not_31_out, S1, S0);
  and and_12 (and_12_out, S4, not_32_out, S2, not_33_out);
  and and_13 (and_13_out, S4, S3, S2, not_34_out, S0, or_1_out);
  or or_2 (or_2_out, and_1_out, and_2_out);
  or or_3 (or_3_out, and_12_out, and_13_out);
  or or_4 (N2, or_2_out, and_3_out, and_4_out, and_5_out, and_6_out, and_7_out, and_8_out, and_9_out, and_10_out, and_11_out, or_3_out);
endmodule

module N3 (
  input  S4,
  input  S3,
  input  S2,
  input  S1,
  input  S0,
  input  try_lt10,
  input  i_lt8,
  output N3
);

  wire and_1_out, and_2_out, and_3_out, and_4_out, and_5_out, and_6_out, and_7_out, and_8_out, and_9_out,
       and_10_out, and_11_out, not_1_out, not_2_out, not_3_out, not_4_out, not_5_out, not_6_out, not_7_out,
       not_8_out, not_9_out, not_10_out, not_11_out, not_12_out, not_13_out, not_14_out, not_15_out,
       not_16_out, not_17_out, not_18_out, not_19_out, not_20_out, not_21_out, not_22_out, not_23_out,
       not_24_out, not_25_out, not_26_out, or_1_out, or_2_out;

  not not_1 (not_1_out, S4);
  not not_2 (not_2_out, S3);
  not not_3 (not_3_out, S2);
  not not_4 (not_4_out, S0);
  not not_5 (not_5_out, S4);
  not not_6 (not_6_out, S3);
  not not_7 (not_7_out, S0);
  not not_8 (not_8_out, try_lt10);
  not not_9 (not_9_out, S3);
  not not_10 (not_10_out, S4);
  not not_11 (not_11_out, S2);
  not not_12 (not_12_out, S0);
  not not_13 (not_13_out, S2);
  not not_14 (not_14_out, S1);
  not not_15 (not_15_out, S0);
  not not_16 (not_16_out, S4);
  not not_17 (not_17_out, S1);
  not not_18 (not_18_out, S4);
  not not_19 (not_19_out, S2);
  not not_20 (not_20_out, S1);
  not not_21 (not_21_out, S2);
  not not_22 (not_22_out, S0);
  not not_23 (not_23_out, S4);
  not not_24 (not_24_out, S3);
  not not_25 (not_25_out, S1);
  not not_26 (not_26_out, S0);
  and and_1 (and_1_out, not_1_out, not_2_out, not_3_out, S1, not_4_out);
  and and_2 (and_2_out, not_5_out, not_6_out, S2, S1, not_7_out, not_8_out);
  and and_3 (and_3_out, not_9_out, S2, S1, S0);
  and and_4 (and_4_out, not_10_out, S3, not_11_out, not_12_out);
  and and_5 (and_5_out, S3, not_13_out, S1, S0);
  and and_6 (and_6_out, S3, S2, not_14_out, not_15_out);
  and and_7 (and_7_out, not_16_out, S3, S2, not_17_out, S0, i_lt8);
  and and_8 (and_8_out, not_18_out, S3, S2, S1);
  and and_9 (and_9_out, S4, S3, not_19_out, not_20_out);
  and and_10 (and_10_out, S4, S3, not_21_out, S1, not_22_out, i_lt8);
  and and_11 (and_11_out, not_23_out, not_24_out, S2, not_25_out, not_26_out);
  or or_1 (or_1_out, and_1_out, and_2_out);
  or or_2 (or_2_out, and_10_out, and_11_out);
  or or_3 (N3, or_1_out, and_3_out, and_4_out, and_5_out, and_6_out, and_7_out, and_8_out, and_9_out, or_2_out);
endmodule

module N4 (
  input  S4,
  input  S3,
  input  S2,
  input  S1,
  input  S0,
  input  found,
  input  try_lt10,
  input  i_lt8,
  output N4
);

  wire and_1_out, and_2_out, and_3_out, and_4_out, and_5_out, and_6_out, and_7_out, and_8_out, and_9_out,
       and_10_out, and_11_out, and_12_out, not_1_out, not_2_out, not_3_out, not_4_out, not_5_out, not_6_out,
       not_7_out, not_8_out, not_9_out, not_10_out, not_11_out, not_12_out, not_13_out, not_14_out,
       not_15_out, not_16_out, not_17_out, not_18_out, not_19_out, not_20_out, not_21_out, not_22_out,
       not_23_out, not_24_out, not_25_out, not_26_out, not_27_out, not_28_out, not_29_out, or_1_out, or_2_out;

  not not_1 (not_1_out, S4);
  not not_2 (not_2_out, S3);
  not not_3 (not_3_out, S2);
  not not_4 (not_4_out, S0);
  not not_5 (not_5_out, S4);
  not not_6 (not_6_out, S3);
  not not_7 (not_7_out, S0);
  not not_8 (not_8_out, try_lt10);
  not not_9 (not_9_out, S4);
  not not_10 (not_10_out, S1);
  not not_11 (not_11_out, i_lt8);
  not not_12 (not_12_out, S3);
  not not_13 (not_13_out, S2);
  not not_14 (not_14_out, S3);
  not not_15 (not_15_out, S1);
  not not_16 (not_16_out, S3);
  not not_17 (not_17_out, S0);
  not not_18 (not_18_out, S3);
  not not_19 (not_19_out, S2);
  not not_20 (not_20_out, S1);
  not not_21 (not_21_out, S2);
  not not_22 (not_22_out, S0);
  not not_23 (not_23_out, S2);
  not not_24 (not_24_out, S1);
  not not_25 (not_25_out, S0);
  not not_26 (not_26_out, S4);
  not not_27 (not_27_out, S3);
  not not_28 (not_28_out, S1);
  not not_29 (not_29_out, S0);
  and and_1 (and_1_out, not_1_out, not_2_out, not_3_out, S1, not_4_out);
  and and_2 (and_2_out, not_5_out, not_6_out, S2, S1, not_7_out, not_8_out);
  and and_3 (and_3_out, not_9_out, S3, S2, not_10_out, S0, not_11_out);
  and and_4 (and_4_out, S4, not_12_out, not_13_out);
  and and_5 (and_5_out, S4, not_14_out, S2, not_15_out);
  and and_6 (and_6_out, S4, not_16_out, S2, S1, not_17_out, found);
  and and_7 (and_7_out, S4, not_18_out, S2, S1, S0);
  and and_8 (and_8_out, S4, S3, not_19_out, not_20_out);
  and and_9 (and_9_out, S4, S3, not_21_out, S1, not_22_out, i_lt8);
  and and_10 (and_10_out, S4, S3, not_23_out, S1, S0);
  and and_11 (and_11_out, S4, S3, S2, not_24_out, not_25_out);
  and and_12 (and_12_out, not_26_out, not_27_out, S2, not_28_out, not_29_out);
  or or_1 (or_1_out, and_1_out, and_2_out);
  or or_2 (or_2_out, and_11_out, and_12_out);
  or or_3 (N4, or_1_out, and_3_out, and_4_out, and_5_out, and_6_out, and_7_out, and_8_out, and_9_out, and_10_out, or_2_out);
endmodule
