// Logisim project Project1_171044032_TurkerTercan.circ as structural Verilog: 12 circuits, main circuit main
module main (
);

  wire B1_out, B2_out, gamelogiccircuit_1_l0, gamelogiccircuit_1_l1, gamelogiccircuit_1_l2,
       gamelogiccircuit_1_l3, gamelogiccircuit_1_l4, gamelogiccircuit_1_l5, gamelogiccircuit_1_l6,
       ledboard_1_b, ledboard_1_bl, ledboard_1_br, ledboard_1_m, ledboard_1_u, ledboard_1_ul, ledboard_1_ur,
       ledboard_2_b, ledboard_2_bl, ledboard_2_br, ledboard_2_m, ledboard_2_u, ledboard_2_ul, ledboard_2_ur,
       LedReset_out, R_out;

  Button B1 (.out(B1_out));
  Button B2 (.out(B2_out));
  Button R (.out(R_out));
  Button LedReset (.out(LedReset_out));
  GameLogicCircuit gamelogiccircuit_1 (
    .B1(B1_out), .B2(B2_out), .R(R_out), .L0(gamelogiccircuit_1_l0), .L1(gamelogiccircuit_1_l1),
    .L2(gamelogiccircuit_1_l2), .L3(gamelogiccircuit_1_l3), .L4(gamelogiccircuit_1_l4),
    .L5(gamelogiccircuit_1_l5), .L6(gamelogiccircuit_1_l6));
  LED L1 (.in(gamelogiccircuit_1_l1));
  LED L2 (.in(gamelogiccircuit_1_l2));
  LED L0 (.in(gamelogiccircuit_1_l0));
  LED L4 (.in(gamelogiccircuit_1_l4));
  LED L5 (.in(gamelogiccircuit_1_l5));
  LED L3 (.in(gamelogiccircuit_1_l3));
  LED L6 (.in(gamelogiccircuit_1_l6));
  LedBoard ledboard_1 (
    .X(gamelogiccircuit_1_l0), .R(LedReset_out), .M(ledboard_1_m), .UL(ledboard_1_ul), .U(ledboard_1_u),
    .UR(ledboard_1_ur), .BR(ledboard_1_br), .B(ledboard_1_b), .BL(ledboard_1_bl));
  LedBoard ledboard_2 (
    .X(gamelogiccircuit_1_l6), .R(LedReset_out), .M(ledboard_2_m), .UL(ledboard_2_ul), .U(ledboard_2_u),
    .UR(ledboard_2_ur), .BR(ledboard_2_br), .B(ledboard_2_b), .BL(ledboard_2_bl));
  _7_Segment_Display u_7_segment_display_1 (
    .g(ledboard_1_m), .f(ledboard_1_ul), .a(ledboard_1_u), .b(ledboard_1_ur), .e(ledboard_1_bl),
    .d(ledboard_1_b), .c(ledboard_1_br));  // open: dp
  _7_Segment_Display u_7_segment_display_2 (
    .g(ledboard_2_m), .f(ledboard_2_ul), .a(ledboard_2_u), .b(ledboard_2_ur), .e(ledboard_2_bl),
    .d(ledboard_2_b), .c(ledboard_2_br));  // open: dp
endmodule

module _2_bit_state_register (
  input  n0,
  input  n1,
  input  Clock,
  output s1,
  output s0
);

  D_Flip_Flop d_ff_1 (.clk(Clock), .D(n1), .Q(s1));  // open: Qn, preset, en, reset
  D_Flip_Flop d_ff_2 (.clk(Clock), .D(n0), .Q(s0));  // open: Qn, preset, en, reset
endmodule

module GameButton (
  input  B,
  output B_Out
);

  wire _2_bit_state_register_s0, _2_bit_state_register_s1, and_1_out, and_2_out, and_3_out, clock_1_out,
       not_1_out, not_2_out, not_3_out, not_4_out, not_5_out, or_1_out;

  Clock clock_1 (.out(clock_1_out));
  _2_bit_state_register _2_bit_state_register (
    .n0(and_3_out), .n1(or_1_out), .Clock(clock_1_out), .s1(_2_bit_state_register_s1),
    .s0(_2_bit_state_register_s0));
  not not_1 (not_1_out, _2_bit_state_register_s1);
  not not_2 (not_2_out, _2_bit_state_register_s0);
  not not_3 (not_3_out, _2_bit_state_register_s1);
  not not_4 (not_4_out, _2_bit_state_register_s0);
  not not_5 (not_5_out, _2_bit_state_register_s1);
  and and_1 (and_1_out, B, not_1_out, _2_bit_state_register_s0);
  and and_2 (and_2_out, B, _2_bit_state_register_s1, not_2_out);
  and and_3 (and_3_out, B, not_3_out, not_4_out);
  and and_4 (B_Out, _2_bit_state_register_s0, not_5_out);
  or or_1 (or_1_out, and_1_out, and_2_out);
endmodule

module _3_bit_state_register (
  input  n2,
  input  n1,
  input  n0,
  input  Clock,
  output s0,
  output s2,
  output s1
);

  D_Flip_Flop d_ff_1 (.clk(Clock), .D(n2), .Q(s2));  // open: Qn, preset, en, reset
  D_Flip_Flop d_ff_2 (.clk(Clock), .D(n1), .Q(s1));  // open: Qn, preset, en, reset
  D_Flip_Flop d_ff_3 (.clk(Clock), .D(n0), .Q(s0));  // open: Qn, preset, en, reset
endmodule

module GameLogicCircuit (
  input  B1,
  input  B2,
  input  R,
  output L0,
  output L1,
  output L2,
  output L3,
  output L4,
  output L5,
  output L6
);

  wire _3_bit_state_register_s0, _3_bit_state_register_s1, _3_bit_state_register_s2, clock_1_out,
       gamebutton_1_b_out, gamebutton_2_b_out, n0_logicgates_1_n0, n1_gates_1_n1, n2_logic_1_n2, not_1_out,
       not_2_out, not_3_out, not_4_out, not_5_out, not_6_out, not_7_out, not_8_out, not_9_out;

  Clock clock_1 (.out(clock_1_out));
  GameButton gamebutton_1 (.B(B1), .B_Out(gamebutton_1_b_out));
  GameButton gamebutton_2 (.B(B2), .B_Out(gamebutton_2_b_out));
  _3_bit_state_register _3_bit_state_register (
    .Clock(clock_1_out), .s2(_3_bit_state_register_s2), .s1(_3_bit_state_register_s1),
    .s0(_3_bit_state_register_s0), .n2(n2_logic_1_n2), .n1(n1_gates_1_n1), .n0(n0_logicgates_1_n0));
  n2_Logic n2_logic_1 (
    .s2(_3_bit_state_register_s2), .s1(_3_bit_state_register_s1), .s0(_3_bit_state_register_s0),
    .B1(gamebutton_1_b_out), .B2(gamebutton_2_b_out), .R(R), .n2(n2_logic_1_n2));
  n1_Gates n1_gates_1 (
    .s2(_3_bit_state_register_s2), .s1(_3_bit_state_register_s1), .s0(_3_bit_state_register_s0),
    .B1(gamebutton_1_b_out), .B2(gamebutton_2_b_out), .R(R), .n1(n1_gates_1_n1));
  n0_LogicGates n0_logicgates_1 (
    .s2(_3_bit_state_register_s2), .s1(_3_bit_state_register_s1), .s0(_3_bit_state_register_s0),
    .B1(gamebutton_1_b_out), .B2(gamebutton_2_b_out), .R(R), .n0(n0_logicgates_1_n0));
  not not_1 (not_1_out, _3_bit_state_register_s2);
  not not_2 (not_2_out, _3_bit_state_register_s2);
  not not_3 (not_3_out, _3_bit_state_register_s0);
  not not_4 (not_4_out, _3_bit_state_register_s2);
  not not_5 (not_5_out, _3_bit_state_register_s1);
  not not_6 (not_6_out, _3_bit_state_register_s1);
  not not_7 (not_7_out, _3_bit_state_register_s0);
  not not_8 (not_8_out, _3_bit_state_register_s1);
  not not_9 (not_9_out, _3_bit_state_register_s0);
  and and_1 (L0, not_1_out, _3_bit_state_register_s1, _3_bit_state_register_s0);
  and and_2 (L1, not_2_out, _3_bit_state_register_s1, not_3_out);
  and and_3 (L2, not_4_out, not_5_out, _3_bit_state_register_s0);
  and and_4 (L3, _3_bit_state_register_s2, not_6_out, not_7_out);
  and and_5 (L4, _3_bit_state_register_s2, not_8_out, _3_bit_state_register_s0);
  and and_6 (L5, _3_bit_state_register_s2, _3_bit_state_register_s1, not_9_out);
  and and_7 (L6, _3_bit_state_register_s2, _3_bit_state_register_s1, _3_bit_state_register_s0);
endmodule

module n2_Logic (
  input  s2,
  input  s1,
  input  s0,
  input  B1,
  input  B2,
  input  R,
  output n2
);

  wire and_1_out, and_2_out, and_3_out, not_1_out, not_2_out, not_3_out, not_4_out, not_5_out, or_1_out,
       or_2_out;

  not not_1 (not_1_out, B1);
  not not_2 (not_2_out, B2);
  not not_3 (not_3_out, B1);
  or or_1 (or_1_out, not_1_out, not_2_out, s0, s1);
  or or_2 (or_2_out, not_3_out, B2, s1, s0);
  not not_4 (not_4_out, s1);
  not not_5 (not_5_out, B1);
  and and_1 (and_1_out, or_1_out, R);
  and and_2 (and_2_out, or_2_out, s2);
  and and_3 (and_3_out, not_4_out, s0, not_5_out, B2);
  or or_3 (n2, and_1_out, and_2_out, and_3_out);
endmodule

module n0_LogicGates (
  input  s2,
  input  s1,
  input  s0,
  input  B1,
  input  B2,
  input  R,
  output n0
);

  wire and_1_out, and_2_out, and_3_out, and_4_out, and_5_out, and_6_out, not_1_out, not_2_out, not_3_out,
       not_4_out, not_5_out, not_6_out, not_7_out, not_8_out, not_9_out;

  not not_1 (not_1_out, R);
  not not_2 (not_2_out, B1);
  not not_3 (not_3_out, B2);
  not not_4 (not_4_out, B1);
  not not_5 (not_5_out, B2);
  not not_6 (not_6_out, s0);
  not not_7 (not_7_out, B1);
  not not_8 (not_8_out, s0);
  not not_9 (not_9_out, B2);
  and and_1 (and_1_out, s0, not_2_out, not_3_out, not_1_out);
  and and_2 (and_2_out, s0, B1, B2, not_1_out);
  and and_3 (and_3_out, s1, not_4_out, B2, not_1_out);
  and and_4 (and_4_out, s1, B1, not_5_out, not_1_out);
  and and_5 (and_5_out, s2, not_6_out, not_7_out, B2, not_1_out);
  and and_6 (and_6_out, s2, not_8_out, B1, not_9_out, not_1_out);
  or or_1 (n0, and_1_out, and_2_out, and_3_out, and_4_out, and_5_out, and_6_out);
endmodule

module n1_Gates (
  input  s2,
  input  s1,
  input  s0,
  input  B1,
  input  B2,
  input  R,
  output n1
);

  wire and_1_out, and_2_out, and_3_out, and_4_out, and_5_out, and_6_out, not_1_out, not_2_out, not_3_out,
       not_4_out, not_5_out, not_6_out, not_7_out, not_8_out, not_9_out, not_10_out, not_11_out, not_12_out;

  not not_1 (not_1_out, s2);
  not not_2 (not_2_out, B2);
  not not_3 (not_3_out, R);
  not not_4 (not_4_out, B1);
  not not_5 (not_5_out, B2);
  not not_6 (not_6_out, R);
  not not_7 (not_7_out, s2);
  not not_8 (not_8_out, R);
  not not_9 (not_9_out, R);
  not not_10 (not_10_out, B1);
  not not_11 (not_11_out, R);
  not not_12 (not_12_out, R);
  and and_1 (and_1_out, not_1_out, s0, B1, not_2_out, not_3_out);
  and and_2 (and_2_out, s1, not_4_out, not_5_out, not_6_out);
  and and_3 (and_3_out, not_7_out, s1, B1, not_8_out);
  and and_4 (and_4_out, s1, s0, not_9_out);
  and and_5 (and_5_out, s2, s0, not_10_out, B2, not_11_out);
  and and_6 (and_6_out, s2, s1, B2, not_12_out);
  or or_1 (n1, and_1_out, and_2_out, and_3_out, and_4_out, and_5_out, and_6_out);
endmodule

module LedBoard (
  input  X,
  input  R,
  output M,
  output UL,
  output U,
  output UR,
  output BR,
  output B,
  output BL
);

  wire clock_1_out, gamebutton_1_b_out, n4_bit_state_register_1_s0, n4_bit_state_register_1_s1,
       n4_bit_state_register_1_s2, n4_bit_state_register_1_s3, ns_ledlogic_1_n0, ns_ledlogic_1_n1,
       ns_ledlogic_1_n2, ns_ledlogic_1_n3;

  GameButton gamebutton_1 (.B(X), .B_Out(gamebutton_1_b_out));
  Clock clock_1 (.out(clock_1_out));
  _4_bit_state_register u_4_bit_state_register_1 (
    .Clock(clock_1_out), .s3(n4_bit_state_register_1_s3), .s2(n4_bit_state_register_1_s2),
    .s1(n4_bit_state_register_1_s1), .s0(n4_bit_state_register_1_s0), .n3(ns_ledlogic_1_n3),
    .n2(ns_ledlogic_1_n2), .n1(ns_ledlogic_1_n1), .n0(ns_ledlogic_1_n0));
  nS_LedLogic ns_ledlogic_1 (
    .s3(n4_bit_state_register_1_s3), .s2(n4_bit_state_register_1_s2), .s1(n4_bit_state_register_1_s1),
    .s0(n4_bit_state_register_1_s0), .R(R), .X(gamebutton_1_b_out), .n3(ns_ledlogic_1_n3),
    .n2(ns_ledlogic_1_n2), .n1(ns_ledlogic_1_n1), .n0(ns_ledlogic_1_n0));
  Lights_Logic lights_logic_1 (
    .s3(n4_bit_state_register_1_s3), .s2(n4_bit_state_register_1_s2), .s1(n4_bit_state_register_1_s1),
    .s0(n4_bit_state_register_1_s0), .M(M), .UL(UL), .U(U), .UR(UR), .BR(BR), .B(B), .BL(BL));
endmodule

module _4_bit_state_register (
  input  n3,
  input  n2,
  input  n1,
  input  n0,
  input  Clock,
  output s0,
  output s3,
  output s2,
  output s1
);

  D_Flip_Flop d_ff_1 (.clk(Clock), .D(n3), .Q(s3));  // open: Qn, preset, en, reset
  D_Flip_Flop d_ff_2 (.clk(Clock), .D(n2), .Q(s2));  // open: Qn, preset, en, reset
  D_Flip_Flop d_ff_3 (.clk(Clock), .D(n1), .Q(s1));  // open: Qn, preset, en, reset
  D_Flip_Flop d_ff_4 (.clk(Clock), .D(n0), .Q(s0));  // open: Qn, preset, en, reset
endmodule

module nS_LedLogic (
  input  s3,
  input  s2,
  input  s1,
  input  s0,
  input  R,
  input  X,
  output n3,
  output n2,
  output n1,
  output n0
);

  wire and_1_out, and_2_out, and_3_out, and_4_out, and_5_out, and_6_out, and_7_out, and_8_out, and_9_out,
       and_10_out, and_11_out, and_12_out, and_13_out, and_14_out, and_15_out, and_16_out, not_1_out,
       not_2_out, not_3_out, not_4_out, not_5_out, not_6_out, not_7_out, not_8_out, not_9_out, not_10_out,
       not_11_out, not_12_out, not_13_out, not_14_out, not_15_out, not_16_out, not_17_out, not_18_out,
       not_19_out, not_20_out, not_21_out, not_22_out;

  not not_1 (not_1_out, R);
  not not_2 (not_2_out, R);
  not not_3 (not_3_out, s2);
  not not_4 (not_4_out, R);
  not not_5 (not_5_out, s1);
  not not_6 (not_6_out, R);
  not not_7 (not_7_out, s0);
  not not_8 (not_8_out, R);
  not not_9 (not_9_out, R);
  not not_10 (not_10_out, X);
  not not_11 (not_11_out, s3);
  not not_12 (not_12_out, s1);
  not not_13 (not_13_out, R);
  not not_14 (not_14_out, s0);
  not not_15 (not_15_out, R);
  not not_16 (not_16_out, R);
  not not_17 (not_17_out, X);
  not not_18 (not_18_out, s0);
  not not_19 (not_19_out, R);
  not not_20 (not_20_out, R);
  not not_21 (not_21_out, X);
  not not_22 (not_22_out, R);
  and and_1 (and_1_out, s2, s1, s0, not_1_out, X);
  and and_2 (and_2_out, s3, not_2_out);
  and and_3 (and_3_out, s3, s2);
  and and_4 (and_4_out, not_3_out, s1, s0, not_4_out, X);
  and and_5 (and_5_out, s2, not_5_out, not_6_out);
  and and_6 (and_6_out, s2, not_7_out, not_8_out);
  and and_7 (and_7_out, s2, not_9_out, not_10_out);
  and and_8 (and_8_out, s3, s2);
  and and_9 (and_9_out, not_11_out, not_12_out, s0, not_13_out, X);
  and and_10 (and_10_out, s1, not_14_out, not_15_out);
  and and_11 (and_11_out, s1, not_16_out, not_17_out);
  and and_12 (and_12_out, s3, s2);
  and and_13 (and_13_out, not_18_out, not_19_out, X);
  and and_14 (and_14_out, s0, not_20_out, not_21_out);
  and and_15 (and_15_out, s3, s0, not_22_out);
  and and_16 (and_16_out, s3, s2);
  or or_1 (n3, and_1_out, and_2_out, and_3_out);
  or or_2 (n2, and_4_out, and_5_out, and_6_out, and_7_out, and_8_out);
  or or_3 (n1, and_9_out, and_10_out, and_11_out, and_12_out);
  or or_4 (n0, and_13_out, and_14_out, and_15_out, and_16_out);
endmodule

module Lights_Logic (
  input  s3,
  input  s2,
  input  s1,
  input  s0,
  output M,
  output UL,
  output U,
  output UR,
  output BR,
  output B,
  output BL
);

  wire and_1_out, and_2_out, and_3_out, and_4_out, and_5_out, and_6_out, and_7_out, and_8_out, and_9_out,
       and_10_out, and_11_out, and_12_out, and_13_out, and_14_out, and_15_out, and_16_out, and_17_out,
       not_1_out, not_2_out, not_3_out, not_4_out, not_5_out, not_6_out, not_7_out, not_8_out, not_9_out,
       not_10_out, not_11_out, not_12_out, not_13_out, not_14_out, not_15_out, not_16_out, not_17_out,
       not_18_out, not_19_out, not_20_out, not_21_out;

  not not_1 (not_1_out, s2);
  and and_1 (and_1_out, not_1_out, s1);
  and and_2 (and_2_out, s2, not_2_out);
  not not_2 (not_2_out, s1);
  and and_3 (and_3_out, s2, not_3_out);
  not not_3 (not_3_out, s0);
  not not_4 (not_4_out, s1);
  and and_4 (and_4_out, not_4_out, not_5_out);
  not not_5 (not_5_out, s0);
  and and_5 (and_5_out, s2, not_6_out);
  not not_6 (not_6_out, s1);
  and and_6 (and_6_out, s2, not_7_out);
  not not_7 (not_7_out, s0);
  not not_8 (not_8_out, s2);
  and and_7 (and_7_out, not_8_out, not_9_out);
  not not_9 (not_9_out, s0);
  and and_8 (and_8_out, s2, s0);
  not not_10 (not_10_out, s2);
  not not_11 (not_11_out, s1);
  and and_9 (and_9_out, not_11_out, not_12_out);
  not not_12 (not_12_out, s0);
  and and_10 (and_10_out, s1, s0);
  not not_13 (not_13_out, s1);
  or or_1 (BR, not_13_out, s0, s2);
  not not_14 (not_14_out, s2);
  and and_11 (and_11_out, not_14_out, not_15_out);
  not not_15 (not_15_out, s0);
  not not_16 (not_16_out, s2);
  and and_12 (and_12_out, not_16_out, s1);
  and and_13 (and_13_out, s1, not_17_out);
  not not_17 (not_17_out, s0);
  not not_18 (not_18_out, s1);
  and and_14 (and_14_out, s2, not_18_out, s0);
  not not_19 (not_19_out, s2);
  and and_15 (and_15_out, not_19_out, not_20_out);
  not not_20 (not_20_out, s0);
  and and_16 (and_16_out, s1, not_21_out);
  not not_21 (not_21_out, s0);
  and and_17 (and_17_out, s3, s2);
  or or_2 (M, and_1_out, and_2_out, and_3_out, s3);
  or or_3 (UL, and_4_out, and_5_out, and_6_out, s3);
  or or_4 (U, and_7_out, s1, and_8_out, s3);
  or or_5 (UR, not_10_out, and_9_out, and_10_out);
  or or_6 (B, and_11_out, and_12_out, and_13_out, and_14_out, s3);
  or or_7 (BL, and_15_out, and_16_out, and_17_out);
endmodule
