// Logisim project 171044032_project2.circ as structural Verilog: 4 circuits, main circuit main
module main (
  input  [15:0] a_in,
  input  [15:0] b_in,
  input  calculate,
  output [31:0] mult,
  output [2:0] states
);

  wire clock_1_out;

  Clock clock_1 (.out(clock_1_out));
  multiplier_FSM Multiplier_FSM_without_Multiplier (
    .calculate(calculate), .clk(clock_1_out), .a_in(a_in), .b_in(b_in), .result(mult), .state(states));
endmodule

module datapath (
  input  load_mult,
  input  [15:0] b_in,
  input  load_b,
  input  [15:0] a_in,
  input  load_a,
  input  select_a,
  input  clk,
  output [31:0] mult_result,
  output a_gt0
);

  wire [15:0] a_q, b_q, bitselector_1_out, multiplexer_1_out;
  wire [31:0] adder_1_out, multiplexer_2_out, multiplexer_3_out;

  Multiplexer #(.width(16), .disabled(0), .enable("false")) multiplexer_1 (
    .in0(a_in), .in1(bitselector_1_out), .out(multiplexer_1_out), .sel(select_a));
  Register #(.width(32)) mult (.D(adder_1_out), .en(load_mult), .Q(mult_result), .clk(clk), .clr(load_b));
  Register #(.width(16)) b (.D(b_in), .en(load_b), .Q(b_q), .clk(clk));  // open: clr
  Register #(.width(16)) a (.D(multiplexer_1_out), .en(load_a), .Q(a_q), .clk(clk));  // open: clr
  Comparator #(.width(16)) comparator_1 (.a(a_q), .b({16{1'b0}}), .gt(a_gt0));  // open: eq, lt
  BitSelector #(.width(32), .group(16)) bitselector_1 (.in(adder_1_out), .out(bitselector_1_out), .sel(1'b0));
  Multiplexer #(.width(32), .disabled(0), .enable("false")) multiplexer_2 (
    .in0(mult_result), .in1({{16{1'b0}}, a_q}), .out(multiplexer_2_out), .sel(select_a));
  Multiplexer #(.width(32), .disabled(0), .enable("false")) multiplexer_3 (
    .in0({{16{1'b0}}, b_q}), .in1({32{1'b1}}), .out(multiplexer_3_out), .sel(select_a));
  Adder #(.width(32)) adder_1 (.a(multiplexer_2_out), .b(multiplexer_3_out), .out(adder_1_out));  // open: cin, cout
endmodule

module control_unit (
  input  calculate,
  input  a_gt0,
  input  clk,
  output load_a,
  output load_b,
  output load_mult,
  output select_a,
  output [2:0] state
);

  wire and_1_out, and_2_out, and_3_out, and_4_out, and_5_out, not_1_out, not_2_out, not_3_out, or_1_out;
  wire [2:0] and_10_out;

  Register #(.width(3)) state_register (.D(and_10_out), .Q(state), .clk(clk));  // open: en, clr
  not not_1 (not_1_out, state[0]);
  not not_2 (not_2_out, state[1]);
  not not_3 (not_3_out, state[2]);
  and and_1 (and_1_out, calculate, not_2_out);
  and and_2 (and_2_out, state[1], a_gt0);
  and and_3 (and_3_out, state[0], not_2_out, not_3_out);
  and and_4 (and_4_out, state[1], a_gt0, not_1_out, not_3_out);
  and and_5 (and_5_out, state[2], not_1_out, not_2_out);
  and and_6 (and_10_out[2], state[0], state[1], not_3_out);
  and and_7 (load_b, not_2_out, not_3_out, state[0]);
  and and_8 (load_mult, state[0], state[1], not_3_out);
  and and_9 (select_a, state[2], not_1_out, not_2_out);
  or or_1 (or_1_out, and_1_out, and_2_out);
  or or_2 (and_10_out[1], and_3_out, and_4_out, and_5_out);
  and and_10 (and_10_out[0], or_1_out, not_1_out, not_3_out);
  or or_3 (load_a, load_b, select_a);

  // Notes on the sheet:
  //   P0
  //   gt0
  //   P2
  //   P1
  //   cal
  //   P0'
  //   P1'
  //   gt0'
  //   P2'
  //   cal'
  //   s1
  //   s3
  //   s4
  //   N0
  //   N1
  //   N2
endmodule

module multiplier_FSM (
  input  [15:0] a_in,
  input  [15:0] b_in,
  input  calculate,
  input  clk,
  output [31:0] result,
  output [2:0] state
);

  wire Control_Unit_load_a, Control_Unit_load_b, Control_Unit_load_mult, Control_Unit_select_a,
       Datapath_a_gt0;

  datapath Datapath (
    .load_mult(Control_Unit_load_mult), .b_in(b_in), .load_b(Control_Unit_load_b), .a_in(a_in),
    .load_a(Control_Unit_load_a), .select_a(Control_Unit_select_a), .clk(clk), .mult_result(result),
    .a_gt0(Datapath_a_gt0));
  control_unit Control_Unit (
    .calculate(calculate), .a_gt0(Datapath_a_gt0), .clk(clk), .load_a(Control_Unit_load_a),
    .load_b(Control_Unit_load_b), .load_mult(Control_Unit_load_mult), .select_a(Control_Unit_select_a),
    .state(state));
endmodule
